# Fritzing sketch NTC10K (saved by Fritzing 0.8.7b)
breadboards: 1

parts:
  Part1 = Arduino Uno (Rev3)
  R1 = Temperature Sensor (Thermistor) [thermistor_type=NTC package=THT]
  R2 = Resistor 10k [package="2010 [SMD]"]
  R3 = Temperature Sensor (Thermistor) [thermistor_type=NTC package=THT]
  R4 = Resistor 10k [package="2010 [SMD]"]

nets:
  N1: Part1.A0, R1.pin_1, R2.Pin_0
  N2: Part1.A5/SCL, R3.pin_1, R4.Pin_0
  N3: Part1.5V, R1.pin_0, R3.pin_0
  N4: Part1.GND, R2.Pin_1, R4.Pin_1

notes:
  NTC 10K Waterproof Temp sensor
  Rain Tank
  NTC 10K Waterproof Temp sensor
  Clean Tank
  Cyan: Analog temp data
  Resistor: 10K ohm

custom parts:
  Resistor 10k: Resistor Basic schematic elements and footprints for 0603, 1206, and PTH resistors.
